# Fritzing sketch Vera_Arduino-Piano 2 (saved by Fritzing 0.9.3b)
circuit board: 8.01982cm x 6.98499cm
breadboards: 1

parts:
  photocell0 = Photocell (LDR) [package=THT]
  photocell1 = Photocell (LDR) [package=THT]
  photocell2 = Photocell (LDR) [package=THT]
  photocell3 = Photocell (LDR) [package=THT]
  photocell4 = Photocell (LDR) [package=THT]
  photocell5 = Photocell (LDR) [package=THT]
  R0 = Resistor [tolerance=±5% resistance=10k package=THT]
  R1 = Resistor [tolerance=±5% resistance=10k package=THT]
  R2 = Resistor [tolerance=±5% resistance=10k package=THT]
  R3 = Resistor [tolerance=±5% resistance=10k package=THT]
  R4 = Resistor [tolerance=±5% resistance=10k package=THT]
  R5 = Resistor [tolerance=±5% resistance=10k package=THT]
  LED0 = LED - 5mm [color="Yellow (595nm)" package="5 mm [THT]"]
  LED1 = LED - 5mm [color="Yellow (595nm)" package="5 mm [THT]"]
  LED2 = LED - 5mm [color="Yellow (595nm)" package="5 mm [THT]"]
  LED3 = LED - 5mm [color="Yellow (595nm)" package="5 mm [THT]"]
  LED4 = LED - 5mm [color="Yellow (595nm)" package="5 mm [THT]"]
  LED5 = LED - 5mm [color="Yellow (595nm)" package="5 mm [THT]"]
  R6 = Resistor [tolerance=±5% resistance=1k package=THT]
  R7 = Resistor [tolerance=±5% resistance=1k package=THT]
  R8 = Resistor [tolerance=±5% resistance=1k package=THT]
  R9 = Resistor [tolerance=±5% resistance=1k package=THT]
  R10 = Resistor [tolerance=±5% resistance=1k package=THT]
  R11 = Resistor [tolerance=±5% resistance=1k package=THT]
  Part1 = Arduino Uno (Rev3)

nets:
  N1: photocell0.pin_0, photocell1.pin_0, photocell2.pin_0, photocell3.pin_0, photocell4.pin_0, photocell5.pin_0, Part1.5V
  N2: photocell0.pin_1, R0.Pin_0, Part1.A0
  N3: photocell1.pin_1, R1.Pin_0, Part1.A1
  N4: photocell2.pin_1, R2.Pin_0, Part1.A2
  N5: photocell3.pin_1, R3.Pin_0, Part1.A3
  N6: photocell4.pin_1, R4.Pin_0, Part1.A4/SDA
  N7: photocell5.pin_1, R5.Pin_0, Part1.A5/SCL
  N8: R0.Pin_1, R1.Pin_1, R2.Pin_1, R3.Pin_1, R4.Pin_1, R5.Pin_1, R6.Pin_1, R7.Pin_1, R8.Pin_1, R9.Pin_1, R10.Pin_1, R11.Pin_1, Part1.GND
  N9: LED0.cathode, R6.Pin_0
  N10: LED0.anode, Part1.D9_PWM
  N11: LED1.cathode, R7.Pin_0
  N12: LED1.anode, Part1.D8
  N13: LED2.cathode, R8.Pin_0
  N14: LED2.anode, Part1.D7
  N15: LED3.cathode, R9.Pin_0
  N16: LED3.anode, Part1.D6_PWM
  N17: LED4.cathode, R10.Pin_0
  N18: LED4.anode, Part1.D5_PWM
  N19: LED5.cathode, R11.Pin_0
  N20: LED5.anode, Part1.D4
